# Fritzing sketch DC Antenna Rotor Controller (saved by Fritzing 0.9.4)
circuit board: 6cm x 4cm
breadboards: 1

parts:
  R2 = Resistor [tolerance=±5% resistance=10k package=THT]
  R12 = Resistor [tolerance=±5% resistance=1k package=THT]
  LED3 = LED - 5mm [color="Red (633nm)" package="5 mm [THT]"]
  Q2 = Basic FET N-Channel [package="TO220 [THT]"]
  D2 = Rectifier Diode [part_number=1N4001 package="300 mil [THT]"]
  D4 = Rectifier Diode [part_number=1N4001 package="300 mil [THT]"]
  DS2Y-5-DC5V3 = DS2Y-5-DC5V [part_number=DS2Y-5-DC5V]
  R13 = Resistor [tolerance=±5% resistance=10k package=THT]
  R15 = Resistor [tolerance=±5% resistance=1k package=THT]
  D5 = Rectifier Diode [part_number=1N4001 package="300 mil [THT]"]
  DS2Y-5-DC5V4 = DS2Y-5-DC5V [part_number=DS2Y-5-DC5V]
  R18 = Resistor [tolerance=±5% resistance=1k package=THT]
  R20 = Resistor [tolerance=±5% resistance=10k package=THT]
  LED5 = LED - 5mm [color="Red (633nm)" package="5 mm [THT]"]
  D6 = Rectifier Diode [part_number=1N4001 package="300 mil [THT]"]
  DS2Y-5-DC5V5 = DS2Y-5-DC5V [part_number=DS2Y-5-DC5V]
  U1 = Voltage Regulator - 5V [package="TO220 [THT]"]
  C1 = Electrolytic Capacitor [capacitance=10µF voltage=50V package="100 mil [THT, electrolytic]"]
  C2 = Electrolytic Capacitor [capacitance=10µF voltage=50V package="100 mil [THT, electrolytic]"]
  LED6 = LED - 5mm [color="Red (633nm)" package="5 mm [THT]"]
  IC1 = ULN2003A [package="DIP16 [THT]"]
  C5 = Ceramic Capacitor [capacitance=100nF package="100 mil [THT, multilayer]"]
  R17 = Resistor [tolerance=±5% resistance=10k package=THT]
  J2 = Camdenboss CTB0158-2 [part_number=CTB0158-2 package=THT]
  JP2 = Header 1 [package=1x01_offset]
  JP3 = Header 1 [package=1x01_offset]
  JP4 = Header 1 [package=1x01_offset]
  JP5 = Header 1 [package=1x01_offset]
  JP6 = Header 1 [package=1x01_offset]
  J3 = Camdenboss CTB0158-4 [part_number=CTB0158-4 package=THT]
  JP7 = Header 1 [package=1x01_offset]
  D7 = Rectifier Diode [part_number=1N4001 package="300 mil [THT]"]
  R21 = Resistor [tolerance=±5% resistance=22k package=THT]

nets:
  GND: R2.Pin_0, Q2.source, D4.anode, R13.Pin_0, DS2Y-5-DC5V4.6_N.C., R20.Pin_0, U1.GND, C1.-, C2.-, IC1.0V, C5.0, R17.Pin_0, JP6.1, J3.pin1, D7.anode
  Vdirection: R2.Pin_1, IC1.In_5, IC1.In_6, JP3.1
  N1: R12.Pin_0, LED3.anode
  12V: R12.Pin_1, D2.cathode, DS2Y-5-DC5V3.1_+, R15.Pin_1, D5.cathode, DS2Y-5-DC5V4.1_+, R18.Pin_1, D6.cathode, DS2Y-5-DC5V5.1_+, U1.input_voltage, C1.+, IC1.COM_-_Common, C5.1, J3.pin3
  N2: LED3.cathode, D2.anode, DS2Y-5-DC5V3.16_-, IC1.Out_6, IC1.Out_5
  Vpwm: Q2.gate, R13.Pin_1, JP2.1, D7.cathode
  N3: Q2.drain, DS2Y-5-DC5V3.8_N.O., DS2Y-5-DC5V3.11_N.C.
  N4: D4.cathode, DS2Y-5-DC5V3.6_N.C., DS2Y-5-DC5V3.9_N.O., DS2Y-5-DC5V4.4_COM
  Motor B: DS2Y-5-DC5V3.4_COM, J2.pin2, R21.Pin_0
  Motor A: DS2Y-5-DC5V3.13_COM, J2.pin1, R21.Pin_1
  N5: R15.Pin_0, LED6.anode
  N6: D5.anode, DS2Y-5-DC5V4.16_-, LED6.cathode, IC1.Out_4, IC1.Out_3
  N7: DS2Y-5-DC5V4.8_N.O., DS2Y-5-DC5V4.9_N.O.
  N8: DS2Y-5-DC5V4.13_COM, DS2Y-5-DC5V5.4_COM
  N9: R18.Pin_0, LED5.anode
  Vdrive: R20.Pin_1, IC1.In_1, IC1.In_2, JP5.1
  N10: LED5.cathode, D6.anode, DS2Y-5-DC5V5.16_-, IC1.Out_2, IC1.Out_1
  48V: DS2Y-5-DC5V5.8_N.O., J3.pin4
  6V: DS2Y-5-DC5V5.6_N.C., J3.pin2
  5V: U1.output_voltage, C2.+, JP7.1
  Venable: IC1.In_3, IC1.In_4, R17.Pin_1, JP4.1
